// Logisim project 1bitregister_test_bench.circ as structural Verilog: 1 circuit, main circuit main
module main (
  input  in_1,
  input  load,
  input  in_3,
  input  in,
  input  in_5,
  input  in_6,
  input  in_7,
  input  in_8,
  output out_9,
  output out_10,
  output out_11,
  output out_12
);

  wire d_ff_1_q, d_ff_1_qn, multiplexer_1_out;

  D_Flip_Flop #(.trigger("low")) d_ff_1 (
    .D(multiplexer_1_out), .Q(d_ff_1_q), .Qn(d_ff_1_qn), .preset(load));  // open: clk, en, reset
  Multiplexer #(.enable("false")) multiplexer_1 (.in0(in), .out(multiplexer_1_out), .sel(load));  // open: in1
  D_Flip_Flop #(.trigger("low")) d_ff_2 (
    .D(in_5), .Q(out_11), .Qn(out_12), .preset(in_6), .en(in_7), .reset(in_8));  // open: clk
  nor nor_1 (out_9, in_1, out_10);
  nor nor_2 (out_10, out_9, in_3);
endmodule
